// Logisim project 2X1 MULTIPLEXER.circ as structural Verilog: 1 circuit, main circuit main
module main (
  input  I0,
  input  I1,
  input  S,
  output Y
);

  wire and_1_out, and_2_out, not_1_out;

  not not_1 (not_1_out, S);
  and and_1 (and_1_out, I0, not_1_out);
  and and_2 (and_2_out, I1, S);
  or or_1 (Y, and_1_out, and_2_out);

  // Notes on the sheet:
  //   2X1 MULTIPLEXER
endmodule
