// Logisim project 4X1 DEMULTIPLEXER.circ as structural Verilog: 1 circuit, main circuit main
module main (
  input  DATA_INPUT,
  input  S0,
  input  S1,
  output D0,
  output D1,
  output D2,
  output D3
);

  wire not_1_out, not_2_out;

  not not_1 (not_1_out, S0);
  not not_2 (not_2_out, S1);
  and and_1 (D0, DATA_INPUT, not_1_out, not_2_out);
  and and_2 (D1, DATA_INPUT, S0, not_2_out);
  and and_3 (D2, DATA_INPUT, not_1_out, S1);
  and and_4 (D3, DATA_INPUT, S1, S0);

  // Notes on the sheet:
  //   4X1 -DEMULTIPLEXER
endmodule
