// Logisim project 8X1 DEMULTIPLEXER.circ as structural Verilog: 1 circuit, main circuit main
module main (
  input  Data_Input,
  input  S2,
  input  S1,
  input  S0,
  output D0,
  output D1,
  output D2,
  output D3,
  output D4,
  output D5,
  output D6,
  output D7
);

  wire not_1_out, not_2_out, not_3_out;

  not not_1 (not_1_out, S1);
  not not_2 (not_2_out, S2);
  not not_3 (not_3_out, S0);
  and and_1 (D0, Data_Input, not_2_out, not_1_out, not_3_out);
  and and_2 (D1, Data_Input, not_2_out, not_1_out, S0);
  and and_3 (D2, Data_Input, not_2_out, S1, not_3_out);
  and and_4 (D3, Data_Input, not_2_out, S1, S0);
  and and_5 (D4, Data_Input, S2, not_1_out, not_3_out);
  and and_6 (D5, Data_Input, S2, not_1_out, S0);
  and and_7 (D6, Data_Input, S2, S1, not_3_out);
  and and_8 (D7, Data_Input, S2, S1, S0);
endmodule
