// Logisim project 8X1 MULTIPLEXER.circ as structural Verilog: 1 circuit, main circuit main
module main (
  input  S2,
  input  D0,
  input  S1,
  input  D1,
  input  S0,
  input  D2,
  input  D3,
  input  D4,
  input  D5,
  input  D6,
  input  D7,
  output out_12
);

  wire D0_out, D1_out, D2_out, D3_out, D4_out, D5_out, D6_out, D7_out, not_1_out, not_2_out, not_3_out,
       not_4_out, not_5_out, not_6_out, not_7_out, not_8_out, not_9_out, not_10_out, not_11_out, not_12_out;

  not not_1 (not_1_out, S2);
  not not_2 (not_2_out, S0);
  not not_3 (not_3_out, S2);
  not not_4 (not_4_out, S2);
  not not_5 (not_5_out, S2);
  not not_6 (not_6_out, S1);
  not not_7 (not_7_out, S0);
  not not_8 (not_8_out, S1);
  not not_9 (not_9_out, S0);
  not not_10 (not_10_out, S1);
  not not_11 (not_11_out, S1);
  not not_12 (not_12_out, S0);
  and u_D0 (D0_out, not_1_out, not_10_out, not_2_out, D0);
  and u_D1 (D1_out, not_3_out, not_11_out, S0, D1);
  and u_D2 (D2_out, not_4_out, S1, not_12_out, D2);
  and u_D3 (D3_out, not_5_out, S1, S0, D3);
  and u_D4 (D4_out, S2, not_6_out, not_7_out, D4);
  and u_D5 (D5_out, S2, not_8_out, S0, D5);
  and u_D6 (D6_out, S2, S1, not_9_out, D6);
  and u_D7 (D7_out, S2, S1, S0, D7);
  or or_1 (out_12, D0_out, D1_out, D2_out, D3_out, D4_out, D5_out, D6_out, D7_out);
endmodule
