// Logisim project BINARY RIPPLE COUNTER WITH DFFS.circ as structural Verilog: 1 circuit, main circuit main
module main (
  input  in_1,
  output Q3
);

  wire clock_1_out, d_ff_1_q, d_ff_1_qn, d_ff_2_q, d_ff_2_qn, d_ff_3_q, d_ff_3_qn, d_ff_4_qn, not_1_out,
       not_2_out, not_3_out, not_4_out, not_5_out, not_6_out, not_7_out, not_8_out;

  Clock clock_1 (.out(clock_1_out));
  not not_1 (not_1_out, clock_1_out);
  D_Flip_Flop #(.trigger("falling")) d_ff_1 (
    .clk(not_1_out), .D(d_ff_1_qn), .Q(d_ff_1_q), .Qn(d_ff_1_qn), .en(not_2_out));  // open: preset, reset
  not not_2 (not_2_out, in_1);
  not not_3 (not_3_out, d_ff_1_q);
  D_Flip_Flop #(.trigger("falling")) d_ff_2 (
    .clk(not_3_out), .D(d_ff_2_qn), .Q(d_ff_2_q), .Qn(d_ff_2_qn), .en(not_4_out));  // open: preset, reset
  not not_4 (not_4_out, in_1);
  not not_5 (not_5_out, d_ff_2_q);
  D_Flip_Flop #(.trigger("falling")) d_ff_3 (
    .clk(not_5_out), .D(d_ff_3_qn), .Q(d_ff_3_q), .Qn(d_ff_3_qn), .en(not_6_out));  // open: preset, reset
  not not_6 (not_6_out, in_1);
  not not_7 (not_7_out, d_ff_3_q);
  D_Flip_Flop #(.trigger("falling")) d_ff_4 (
    .clk(not_7_out), .D(d_ff_4_qn), .Q(Q3), .Qn(d_ff_4_qn), .en(not_8_out));  // open: preset, reset
  not not_8 (not_8_out, in_1);

  // Notes on the sheet:
  //   BINARY RIPPLE COUNTER WITH DFFS
endmodule
