// Logisim project BINARY RIPPLE UP COUNTER TFFS.circ as structural Verilog: 1 circuit, main circuit main
module main (
  input  in_1,
  output out_2,
  output out_3,
  output out_4
);

  wire clock_1_out;

  Clock clock_1 (.out(clock_1_out));
  T_Flip_Flop #(.trigger("falling")) t_ff_1 (.clk(clock_1_out), .T(in_1), .Q(out_3));  // open: Qn, preset, reset, en
  T_Flip_Flop #(.trigger("falling")) t_ff_2 (.clk(out_3), .T(in_1), .Q(out_4));  // open: Qn, preset, reset, en
  T_Flip_Flop #(.trigger("falling")) t_ff_3 (.clk(out_4), .T(in_1), .Q(out_2));  // open: Qn, preset, reset, en

  // Notes on the sheet:
  //   BINARY RIPPLE WITH UP COUNTER -TFFS
endmodule
