// Logisim project BINARY RIPPLE WITH UP JK FFS.circ as structural Verilog: 1 circuit, main circuit main
module main (
  input  _1,
  output Q0,
  output Q1,
  output Q2,
  output Q3
);

  wire CLK_out, not_1_out, not_2_out, not_3_out, not_4_out;

  Clock CLK (.out(CLK_out));
  not not_1 (not_1_out, CLK_out);
  J_K_Flip_Flop #(.trigger("falling")) j_k_ff_1 (
    .J(_1), .clk(not_1_out), .K(_1), .Q(Q0));  // open: Qn, preset, en, reset
  not not_2 (not_2_out, Q0);
  J_K_Flip_Flop #(.trigger("falling")) j_k_ff_2 (
    .J(_1), .clk(not_2_out), .K(_1), .Q(Q1));  // open: Qn, preset, en, reset
  not not_3 (not_3_out, Q1);
  J_K_Flip_Flop #(.trigger("falling")) j_k_ff_3 (
    .J(_1), .clk(not_3_out), .K(_1), .Q(Q2));  // open: Qn, preset, en, reset
  not not_4 (not_4_out, Q2);
  J_K_Flip_Flop #(.trigger("falling")) j_k_ff_4 (
    .J(_1), .clk(not_4_out), .K(_1), .Q(Q3));  // open: Qn, preset, en, reset

  // Notes on the sheet:
  //   BINARY RIPPLE WITH UP COUNTER-JK FFS OR FOUR BIT UP COUNTER
endmodule
