// Logisim project BINARY TO GREY CODE.circ as structural Verilog: 1 circuit, main circuit main
module main (
  input  b0,
  input  b1,
  input  b2,
  input  b3,
  output g0,
  output g1,
  output g2,
  output g3
);

  xor xor_1 (g0, b0, b1);
  xor xor_2 (g1, b1, b2);
  xor xor_3 (g2, b2, b3);

  assign g3 = b3;

  // Notes on the sheet:
  //   binary to grey code
endmodule
