// Logisim project D FLIP FLOP.circ as structural Verilog: 1 circuit, main circuit main
module main (
  input  D,
  output Q,
  output QB
);

  wire CLK_out, nand_1_out, nand_2_out, not_1_out;

  not not_1 (not_1_out, D);
  Clock CLK (.out(CLK_out));
  nand nand_1 (nand_1_out, D, CLK_out);
  nand nand_2 (nand_2_out, CLK_out, not_1_out);
  nand nand_3 (Q, nand_1_out, QB);
  nand nand_4 (QB, Q, nand_2_out);

  // Notes on the sheet:
  //   D FLIP FLOP
endmodule
