// Logisim project DECODER.circ as structural Verilog: 1 circuit, main circuit main
module main (
  input  X,
  input  Y,
  input  Z,
  output D0,
  output D1,
  output D2,
  output D3,
  output D4,
  output D5,
  output D6,
  output D7
);

  wire and_1_out, and_3_out, and_4_out, and_5_out, and_6_out, and_7_out, and_8_out, not_1_out, not_2_out,
       not_3_out, not_4_out, not_5_out, not_6_out, not_7_out, not_8_out, not_9_out, not_10_out, not_11_out,
       not_12_out;

  not not_1 (not_1_out, X);
  not not_2 (not_2_out, Y);
  not not_3 (not_3_out, X);
  not not_4 (not_4_out, Y);
  not not_5 (not_5_out, X);
  not not_6 (not_6_out, X);
  not not_7 (not_7_out, Y);
  not not_8 (not_8_out, Y);
  and and_1 (and_1_out, X, Y);
  not not_9 (not_9_out, Z);
  and and_2 (D7, X, Z);
  and and_3 (and_3_out, not_1_out, not_2_out);
  not not_10 (not_10_out, Z);
  and and_4 (and_4_out, not_3_out, not_4_out);
  and and_5 (and_5_out, not_5_out, Y);
  not not_11 (not_11_out, Z);
  and and_6 (and_6_out, not_6_out, Y);
  and and_7 (and_7_out, X, not_7_out);
  not not_12 (not_12_out, Z);
  and and_8 (and_8_out, X, not_8_out);
  and and_9 (D6, and_1_out, not_9_out);
  and and_10 (D0, and_3_out, not_10_out);
  and and_11 (D1, and_4_out, Z);
  and and_12 (D2, and_5_out, not_11_out);
  and and_13 (D3, and_6_out, Z);
  and and_14 (D4, and_7_out, not_12_out);
  and and_15 (D5, and_8_out, Z);
endmodule
