// Logisim project ENCODER.circ as structural Verilog: 1 circuit, main circuit main
module main (
  input  d6,
  input  d7,
  input  d5,
  input  d4,
  input  d3,
  input  d2,
  input  d1,
  output x,
  output y,
  output z
);

  or or_1 (x, d7, d6, d5, d4);
  or or_2 (y, d7, d6, d3, d2);
  or or_3 (z, d7, d5, d3, d1);
endmodule
