// Logisim project FULL_ADDER.circ as structural Verilog: 5 circuits, main circuit main
module main (
  input  X,
  input  in_2,
  input  Z,
  output SUM,
  output CARRY
);

  wire and_1_out, and_2_out, and_3_out, xor_1_out;

  xor xor_1 (xor_1_out, X, in_2);
  and and_1 (and_1_out, X, in_2);
  and and_2 (and_2_out, in_2, Z);
  and and_3 (and_3_out, Z, X);
  xor xor_2 (SUM, xor_1_out, Z);
  or or_1 (CARRY, and_1_out, and_2_out, and_3_out);

  // Notes on the sheet:
  //   FULL ADDER
endmodule

module BINARY_SUBTRACTOR (
  input  in_1,
  input  in_2,
  input  in_3,
  input  in_4,
  input  in_5,
  input  in_6,
  input  in_7,
  input  in_8,
  input  FA,
  output out_10,
  output out_11,
  output out_12,
  output out_13,
  output out_14
);

  wire main_2_carry, main_3_carry, main_4_carry, not_1_out, not_2_out, not_3_out, not_4_out;

  not not_1 (not_1_out, in_1);
  main main_1 (.X(main_2_carry), .in_2(not_1_out), .Z(in_6), .SUM(out_11), .CARRY(out_10));
  not not_2 (not_2_out, in_2);
  main main_2 (.X(main_3_carry), .in_2(not_2_out), .Z(in_7), .SUM(out_12), .CARRY(main_2_carry));
  not not_3 (not_3_out, in_3);
  main main_3 (.X(main_4_carry), .in_2(not_3_out), .Z(in_8), .SUM(out_13), .CARRY(main_3_carry));
  not not_4 (not_4_out, in_4);
  main main_4 (.X(FA), .in_2(not_4_out), .Z(in_5), .SUM(out_14), .CARRY(main_4_carry));

  // Notes on the sheet:
  //   FA
  //   FA
  //   FA
endmodule

module BINARY_ADDER_SUBTRACTOR (
  input  in_1,
  input  in_2,
  input  in_3,
  input  in_4,
  input  in_5,
  input  in_6,
  input  in_7,
  input  in_8,
  input  in_9,
  output out_10,
  output out_11,
  output out_12,
  output out_13,
  output out_14
);

  wire main_2_carry, main_3_carry, main_4_carry, xor_1_out, xor_2_out, xor_3_out, xor_4_out;

  xor xor_1 (xor_1_out, in_1, in_9);
  main main_1 (.X(main_2_carry), .in_2(in_2), .Z(xor_1_out), .SUM(out_11), .CARRY(out_10));
  xor xor_2 (xor_2_out, in_3, in_9);
  main main_2 (.X(main_3_carry), .in_2(in_4), .Z(xor_2_out), .SUM(out_12), .CARRY(main_2_carry));
  xor xor_3 (xor_3_out, in_5, in_9);
  xor xor_4 (xor_4_out, in_7, in_9);
  main main_3 (.X(main_4_carry), .in_2(in_6), .Z(xor_3_out), .SUM(out_13), .CARRY(main_3_carry));
  main main_4 (.X(in_9), .in_2(in_8), .Z(xor_4_out), .SUM(out_14), .CARRY(main_4_carry));

  // Notes on the sheet:
  //   FA
  //   FA
  //   BINARY ADDER SUBTRACTOR
  //   FA
  //   FA
endmodule

module BINARY_ADDER (
  input  B0,
  input  B3,
  input  B2,
  input  B1,
  input  in_5,
  input  in_6,
  input  in_7,
  input  A0,
  input  C0,
  output out_10,
  output out_11,
  output out_12,
  output out_13,
  output out_14
);

  wire FULL_ADDER_2_sum, FULL_ADDER_3_sum;

  main FUll_ADDER (.X(B3), .in_2(FULL_ADDER_2_sum), .Z(in_5), .SUM(out_10), .CARRY(out_11));
  main FULL_ADDER_2 (.X(B2), .in_2(FULL_ADDER_3_sum), .Z(in_6), .SUM(FULL_ADDER_2_sum), .CARRY(out_12));
  main FULL_ADDER_3 (.X(B1), .in_2(B1), .Z(in_7), .SUM(FULL_ADDER_3_sum), .CARRY(out_13));
  main FULL_ADDER_4 (.X(C0), .in_2(A0), .Z(B0), .SUM(out_14), .CARRY(B1));

  // Notes on the sheet:
  //   A3
  //   BINARY ADDER
  //   A2
  //   A1
endmodule

module BINARY_MULTIPLIER (
  input  A3,
  input  A2,
  input  A1,
  input  A0,
  input  B0,
  input  A2_2,
  input  A1_2,
  input  A0_2,
  input  in_9,
  input  B1,
  input  X1,
  input  _0,
  input  A3_2,
  input  A1_3,
  input  A0_3,
  input  in_16,
  input  B2,
  input  _0_2,
  input  A3_3,
  input  A0_4,
  input  A2_3,
  input  A1_4,
  input  B3,
  input  _0_3,
  output out_25,
  output out_26,
  output out_27,
  output out_28,
  output out_29,
  output out_30,
  output out_31,
  output out_32
);

  wire and_1_out, and_2_out, and_3_out, and_4_out, and_5_out, and_6_out, and_7_out, and_8_out, and_9_out,
       and_10_out, and_11_out, and_12_out, and_13_out, and_14_out, and_16_out, binary_adder_1_out_10,
       binary_adder_1_out_11, binary_adder_1_out_12, binary_adder_1_out_13, binary_adder_2_out_10,
       binary_adder_2_out_11, binary_adder_2_out_12, binary_adder_2_out_13;

  and and_1 (and_1_out, B2, A3_2);
  and and_2 (and_2_out, B3, A3_3);
  and and_3 (and_3_out, B1, A2_2);
  and and_4 (and_4_out, B2, A1_3);
  and and_5 (and_5_out, B3, A2_3);
  and and_6 (and_6_out, B0, A3);
  and and_7 (and_7_out, B1, A1_2);
  BINARY_ADDER binary_adder_1 (
    .in_5(X1), .B3(and_3_out), .in_6(and_6_out), .B2(and_7_out), .in_7(and_12_out), .B1(and_13_out),
    .out_10(binary_adder_1_out_10), .out_11(binary_adder_1_out_11), .out_12(binary_adder_1_out_12),
    .out_13(binary_adder_1_out_13), .out_14(out_28), .B0(and_11_out), .A0(and_16_out), .C0(_0));
  and and_8 (and_8_out, B2, in_16);
  and and_9 (and_9_out, B2, A0_3);
  BINARY_ADDER binary_adder_2 (
    .in_5(binary_adder_1_out_10), .B3(and_1_out), .in_6(and_4_out), .B2(binary_adder_1_out_11),
    .in_7(and_9_out), .B1(binary_adder_1_out_12), .out_10(binary_adder_2_out_10),
    .out_11(binary_adder_2_out_11), .out_12(binary_adder_2_out_12), .out_13(binary_adder_2_out_13),
    .out_14(out_27), .B0(and_8_out), .A0(binary_adder_1_out_13), .C0(_0_2));
  and and_10 (and_10_out, B3, A1_4);
  BINARY_ADDER binary_adder_3 (
    .in_5(and_2_out), .B3(binary_adder_2_out_10), .in_6(and_5_out), .B2(binary_adder_2_out_11),
    .in_7(and_10_out), .B1(binary_adder_2_out_12), .out_10(out_25), .out_11(out_30), .out_12(out_31),
    .out_13(out_32), .out_14(out_26), .B0(and_14_out), .A0(binary_adder_2_out_13), .C0(_0_3));
  and and_11 (and_11_out, B0, A1);
  and and_12 (and_12_out, B0, A2);
  and and_13 (and_13_out, B1, A0_2);
  and and_14 (and_14_out, B3, A0_4);
  and and_15 (out_29, B0, A0);
  and and_16 (and_16_out, B1, in_9);

  // Notes on the sheet:
  //   A3
  //   BA
  //   A2
  //   BA
  //   BA
endmodule
