// Logisim project GATED D LATCH.circ as structural Verilog: 1 circuit, main circuit main
module main (
  input  EN,
  input  D,
  output Q,
  output Q_prime
);

  wire and_1_out, and_2_out, not_1_out;

  not not_1 (not_1_out, D);
  and and_1 (and_1_out, not_1_out, EN);
  and and_2 (and_2_out, EN, D);
  nor nor_1 (Q, and_1_out, Q_prime);
  nor nor_2 (Q_prime, Q, and_2_out);

  // Notes on the sheet:
  //   D LATCH
endmodule
