// Logisim project GATED SR LATCH.circ as structural Verilog: 1 circuit, main circuit main
module main (
  input  S,
  input  EN,
  input  R,
  output Q,
  output QBAR
);

  wire nand_1_out, nand_2_out, not_1_out, not_2_out, not_3_out, not_4_out;

  nand nand_1 (nand_1_out, S, EN);
  nand nand_2 (nand_2_out, EN, R);
  not not_1 (not_1_out, nand_1_out);
  not not_2 (not_2_out, QBAR);
  not not_3 (not_3_out, Q);
  not not_4 (not_4_out, nand_2_out);
  or or_1 (Q, not_1_out, not_2_out);
  or or_2 (QBAR, not_3_out, not_4_out);

  // Notes on the sheet:
  //   GATED SR LATCH
endmodule
