// Logisim project GATES.circ as structural Verilog: 1 circuit, main circuit main
module main (
  input  in_1,
  input  in_2,
  input  in_3,
  input  in_4,
  input  in_5,
  input  in_6,
  input  in_7,
  input  in_8,
  input  in_9,
  input  in_10,
  input  in_11,
  input  in_12,
  input  in_13,
  input  in_14,
  output out_15,
  output out_16,
  output out_17,
  output out_18,
  output out_19,
  output out_20,
  output out_21,
  output out_22
);

  wire buffer_1_out;

  and AND (out_16, in_2, in_5);
  nand NAND (out_20, in_8, in_11);
  xnor XNOR (out_22, in_12, in_14);
  not not_1 (out_17, in_3);
  nor NOR (out_18, in_6, in_9);
  buf buffer_1 (buffer_1_out, in_13);
  buf buffer_2 (out_21, buffer_1_out);
  or OR (out_15, in_1, in_4);
  xor XOR (out_19, in_7, in_10);

  // Notes on the sheet:
  //   XNOR GATE
  //   AND GATE
  //   NAND GATE
  //   NOT GATE
  //   NOR GATE
  //   BUFFER 
  //   OR GATE
  //   XOR GATE
endmodule
