// Logisim project GREY CODE TO BINARY.circ as structural Verilog: 1 circuit, main circuit main
module main (
  input  G0,
  input  G1,
  input  G2,
  input  G3,
  output B0,
  output B1,
  output B2,
  output B3
);

  xor xor_1 (B0, G0, B1);
  xor xor_2 (B1, G1, B2);
  xor xor_3 (B2, G2, G3);

  assign B3 = G3;

  // Notes on the sheet:
  //   GREY CODE TO BINARY
endmodule
