// Logisim project HALF SUBTRACTOR.circ as structural Verilog: 1 circuit, main circuit main
module main (
  input  in_1,
  input  in_2,
  output out_3,
  output out_4
);

  wire not_1_out;

  not not_1 (not_1_out, in_1);
  xor xor_1 (out_3, in_1, in_2);
  and and_1 (out_4, in_2, not_1_out);

  // Notes on the sheet:
  //   HALF SUBTRACTOR
endmodule
