// Logisim project HALF_ADDER.circ as structural Verilog: 2 circuits, main circuit main
// HALF ADDER
module main (
  input  x,
  input  y,
  output sum,
  output carry
);

  xor xor_1 (sum, x, y);
  and and_1 (carry, x, y);

  // Notes on the sheet:
  //   HALF ADDER
endmodule

module HALF_ADDER_BLOCK (
  input  in_1,
  input  in_2,
  input  in_3,
  output CARRY,
  output SUM
);

  wire main_1_carry, main_1_sum, main_2_carry;

  main main_1 (.x(in_1), .y(in_2), .sum(main_1_sum), .carry(main_1_carry));
  main main_2 (.x(main_1_sum), .y(in_3), .sum(SUM), .carry(main_2_carry));
  or or_1 (CARRY, main_1_carry, main_2_carry);

  // Notes on the sheet:
  //   FULL ADDER USING HALF ADDER BLOCKS
endmodule
