// Logisim project PARITY CHECKER.circ as structural Verilog: 1 circuit, main circuit main
module main (
  input  X,
  input  Y,
  input  Z,
  input  P,
  output C
);

  wire xor_1_out, xor_2_out;

  xor xor_1 (xor_1_out, X, Y);
  xor xor_2 (xor_2_out, Z, P);
  xor xor_3 (C, xor_1_out, xor_2_out);

  // Notes on the sheet:
  //   PARITY GENERATOR
endmodule
