// Logisim project PARITY_GENERATOR.circ as structural Verilog: 1 circuit, main circuit main
module main (
  input  x,
  input  y,
  input  z,
  output p
);

  wire xor_1_out;

  xor xor_1 (xor_1_out, x, y);
  xor xor_2 (p, xor_1_out, z);

  // Notes on the sheet:
  //   PARITY GENERATOR
endmodule
