// Logisim project RIPPLE DOWN COUNTER.circ as structural Verilog: 1 circuit, main circuit main
module main (
  input  in_1,
  input  in_2,
  input  in_3,
  output out_4,
  output out_5,
  output out_6,
  output out_7
);

  wire clock_1_out, not_1_out, not_2_out, not_3_out, t_ff_1_qn, t_ff_2_qn;

  not not_1 (not_1_out, clock_1_out);
  Clock clock_1 (.out(clock_1_out));
  T_Flip_Flop #(.trigger("falling")) t_ff_1 (
    .clk(not_1_out), .T(in_1), .Q(out_6), .Qn(t_ff_1_qn));  // open: preset, reset, en
  not not_2 (not_2_out, t_ff_1_qn);
  T_Flip_Flop #(.trigger("falling")) t_ff_2 (
    .clk(not_2_out), .T(in_2), .Q(out_4), .Qn(t_ff_2_qn));  // open: preset, reset, en
  not not_3 (not_3_out, t_ff_2_qn);
  T_Flip_Flop #(.trigger("falling")) t_ff_3 (
    .clk(not_3_out), .T(in_3), .Q(out_5), .Qn(out_7));  // open: preset, reset, en

  // Notes on the sheet:
  //   RIPPLE DOWN COUNTER
endmodule
