// Logisim project RIPPLE UP-DOWN COUNTER.circ as structural Verilog: 1 circuit, main circuit main
module main (
  input  in_1,
  input  in_2,
  input  in_3,
  input  in_4,
  input  in_5,
  input  in_6,
  input  in_7,
  output out_8,
  output out_9
);

  wire and_1_out, and_2_out, and_3_out, and_4_out, clock_1_out, j_k_ff_1_q, j_k_ff_1_qn, j_k_ff_2_q,
       j_k_ff_2_qn, not_1_out, not_2_out, not_3_out, not_4_out, or_1_out, or_2_out;

  not not_1 (not_1_out, clock_1_out);
  Clock clock_1 (.out(clock_1_out));
  not not_2 (not_2_out, in_7);
  J_K_Flip_Flop j_k_ff_1 (
    .J(in_1), .clk(not_1_out), .K(in_4), .Q(j_k_ff_1_q), .Qn(j_k_ff_1_qn));  // open: preset, en, reset
  and and_1 (and_1_out, j_k_ff_1_q, in_7);
  and and_2 (and_2_out, not_2_out, j_k_ff_1_qn);
  not not_3 (not_3_out, or_1_out);
  or or_1 (or_1_out, and_1_out, and_2_out);
  J_K_Flip_Flop j_k_ff_2 (
    .J(in_2), .clk(not_3_out), .K(in_5), .Q(j_k_ff_2_q), .Qn(j_k_ff_2_qn));  // open: preset, en, reset
  and and_3 (and_3_out, j_k_ff_2_q, in_7);
  and and_4 (and_4_out, not_2_out, j_k_ff_2_qn);
  or or_2 (or_2_out, and_3_out, and_4_out);
  not not_4 (not_4_out, or_2_out);
  J_K_Flip_Flop j_k_ff_3 (.J(in_3), .clk(not_4_out), .K(in_6), .Q(out_8), .Qn(out_9));  // open: preset, en, reset

  // Notes on the sheet:
  //   RIPPLE UP-DOWN COUNTER
endmodule
