// Logisim project SR LATCHHIGH AND LOW ACTIVE.circ as structural Verilog: 1 circuit, main circuit main
module main (
  input  SBAR,
  input  RBAR,
  input  R,
  input  S,
  output Q,
  output QBBAR,
  output Q_2,
  output QBAR
);

  nor nor_1 (Q_2, R, QBAR);
  nor nor_2 (QBAR, Q_2, S);
  nand nand_1 (Q, SBAR, QBBAR);
  nand nand_2 (QBBAR, Q, RBAR);

  // Notes on the sheet:
  //   ACTIVE LOW LATCH SR
  //   ACTIVE HIGH LATCH SR
endmodule
